// Logisim project 1lab.circ as structural Verilog: 1 circuit, main circuit main
module main (
  input  X1,
  input  X2,
  output out_3,
  output out_4,
  output out_5
);

  wire and_1_out, and_2_out, and_3_out, and_4_out, and_5_out, and_6_out, and_7_out, button_1_out,
       clock_1_out, d_ff_1_q, d_ff_2_q, not_1_out, not_2_out, not_3_out, not_4_out, not_5_out, not_6_out,
       not_7_out, not_8_out, not_9_out, not_10_out, not_11_out, not_12_out, not_13_out, or_1_out, or_2_out;

  not not_1 (not_1_out, d_ff_1_q);
  not not_2 (not_2_out, d_ff_2_q);
  not not_3 (not_3_out, X1);
  not not_4 (not_4_out, X2);
  not not_5 (not_5_out, d_ff_1_q);
  not not_6 (not_6_out, d_ff_2_q);
  not not_7 (not_7_out, d_ff_1_q);
  not not_8 (not_8_out, X1);
  not not_9 (not_9_out, d_ff_2_q);
  not not_10 (not_10_out, X2);
  not not_11 (not_11_out, X2);
  and and_1 (and_1_out, not_1_out, d_ff_2_q, X1);
  and and_2 (and_2_out, d_ff_1_q, not_2_out, not_3_out, not_4_out);
  or or_1 (or_1_out, and_1_out, and_2_out, and_3_out);
  and and_3 (and_3_out, d_ff_1_q, d_ff_2_q, X2);
  and and_4 (and_4_out, not_5_out, not_6_out);
  and and_5 (and_5_out, not_7_out, not_8_out, d_ff_2_q);
  and and_6 (and_6_out, d_ff_1_q, not_9_out, not_10_out, X1);
  and and_7 (and_7_out, d_ff_1_q, d_ff_2_q, not_11_out);
  Clock clock_1 (.out(clock_1_out));
  or or_2 (or_2_out, and_4_out, and_5_out, and_6_out, and_7_out);
  Button button_1 (.out(button_1_out));
  D_Flip_Flop d_ff_1 (.clk(clock_1_out), .D(or_1_out), .Q(d_ff_1_q), .reset(button_1_out));  // open: Qn, preset, en
  D_Flip_Flop d_ff_2 (.clk(clock_1_out), .D(or_2_out), .Q(d_ff_2_q), .reset(button_1_out));  // open: Qn, preset, en
  not not_12 (not_12_out, d_ff_1_q);
  and and_8 (out_3, not_12_out, d_ff_2_q);
  and and_9 (out_4, d_ff_1_q, not_13_out);
  not not_13 (not_13_out, d_ff_2_q);
  and and_10 (out_5, d_ff_1_q, d_ff_2_q);
endmodule
